# Fritzing sketch Atelier0 (saved by Fritzing 0.9.3b)
breadboards: 1

parts:
  Composant1 = Arduino Uno (Rev3)
  VCC1 = 4 x AAA Battery Mount
  R1 = Rotary Potentiometer (Small) [maximum_resistance=100kΩ package=THT]
  J1 = Basic Servo
  J2 = Piezo Speaker
  LED1 = LED - 5mm [color="Red (633nm)" package="5 mm [THT]"]
  R2 = Resistor [tolerance=±5% resistance=220 package=THT]

nets:
  N1: Composant1.A0, R1.wiper
  N2: Composant1.D3_PWM, J2.pin2
  N3: Composant1.D4, J1.pulse
  N4: Composant1.D5_PWM, LED1.anode
  N5: VCC1.-, R1.leg2, J1.gnd, J2.pin1, R2.Pin_1
  N6: VCC1.+, J1.vcc
  N7: LED1.cathode, R2.Pin_0
