# Fritzing sketch SchemaRGB (saved by Fritzing 0.9.3b)
breadboards: 1

parts:
  LED1 = RGB LED (com. cathode, rgb) [package="5 mm [THT]"]
  R3 = Resistor [tolerance=±5% resistance=220 package=THT]
  Composant1 = Arduino Uno (Rev3)
  R1 = Resistor [tolerance=±5% resistance=220 package=THT]
  R2 = Resistor [tolerance=±5% resistance=220 package=THT]

nets:
  N1: LED1.red_anode, R3.Pin_0
  N2: LED1.green_anode, R2.Pin_0
  N3: LED1.blue_anode, R1.Pin_0
  N4: R3.Pin_1, Composant1.D7
  N5: Composant1.D5_PWM, R1.Pin_1
  N6: Composant1.D6_PWM, R2.Pin_1
