# Fritzing sketch SchemaRGBBuz (saved by Fritzing 0.9.3b)
breadboards: 1

parts:
  LED1 = RGB LED (com. cathode, rgb) [package="5 mm [THT]"]
  Composant1 = Arduino Uno (Rev3)
  R4 = Rotary Potentiometer (Small) [maximum_resistance=100kΩ package=THT]  # not connected
  R6 = Resistor [tolerance=±5% resistance=220 package=THT]
  R5 = Resistor [tolerance=±5% resistance=220 package=THT]
  R7 = Resistor [tolerance=±5% resistance=220 package=THT]
  J1 = Piezo Speaker

nets:
  N1: LED1.red_anode, R7.Pin_0
  N2: LED1.common_cathode, Composant1.GND, J1.pin1
  N3: LED1.green_anode, R6.Pin_0
  N4: LED1.blue_anode, R5.Pin_0
  N5: Composant1.D3_PWM, J1.pin2
  N6: Composant1.D5_PWM, R7.Pin_1
  N7: Composant1.D6_PWM, R6.Pin_1
  N8: Composant1.D7, R5.Pin_1
