# Fritzing sketch SchemaRGBBuzPotServ (saved by Fritzing 0.9.3b)
breadboards: 1

parts:
  LED1 = RGB LED (com. cathode, rgb) [package="5 mm [THT]"]
  Composant1 = Arduino Uno (Rev3)
  R4 = Rotary Potentiometer (Small) [maximum_resistance=100kΩ package=THT]
  R6 = Resistor [tolerance=±5% resistance=220 package=THT]
  R5 = Resistor [tolerance=±5% resistance=220 package=THT]
  R7 = Resistor [tolerance=±5% resistance=220 package=THT]
  J1 = Piezo Speaker
  J2 = Basic Servo

nets:
  N1: LED1.red_anode, R7.Pin_0
  GND: LED1.common_cathode, Composant1.GND, R4.leg2, J1.pin1, J2.gnd
  N2: LED1.green_anode, R6.Pin_0
  N3: LED1.blue_anode, R5.Pin_0
  N4: Composant1.A0, R4.wiper
  N5: Composant1.D9_PWM, J2.pulse
  N6: Composant1.D3_PWM, J1.pin2
  N7: Composant1.D5_PWM, R7.Pin_1
  N8: Composant1.D6_PWM, R6.Pin_1
  N9: Composant1.D7, R5.Pin_1
  5V: Composant1.5V, R4.leg1, J2.vcc
